# Fritzing sketch wall-e_radio (saved by Fritzing 0.9.3b)
breadboards: 1

parts:
  Part1 = Arduino Nano (Rev3.0) (ICSP)
  BAT1 = BC9VPC [package=bc9vpc]
  U1 = L9110 H-bridge module [part_number="L9110 H-bridge"]
  Part2 = NRF24L01+ Breakout Board

nets:
  GND: Part1.GND, BAT1.V-, U1.GND, Part2.GND
  N1: Part1.D2, Part2.CE
  N2: Part1.D4, Part2.CS
  N3: Part1.D5, U1.A-IA
  N4: Part1.D6, U1.B-IA
  N5: Part1.D7, U1.A-IB
  N6: Part1.D8, U1.B-IB
  N7: Part1.D11/MOSI, Part2.MOSI
  N8: Part1.D12/MISO, Part2.MISO
  VIN: Part1.VIN, BAT1.V+, U1.VCC
  5V: Part1.5V, Part2.VCC
  N9: Part1.D13/SCK, Part2.SCK
